# Fritzing sketch WiringDiagram (saved by Fritzing 1.0.4)
breadboards: 1

parts:
  A1 = Werner Rothschopf (modified to ESP32-S3-DevKitC dual USB by vanepp Aug 2024)
  L1 = sct-013 [part_number=sct-013 package="4Ucon 08780 [THT]"]
  Part2 = ADS1115
  A2 = 2-Channel 5v Relay Shield [package=relay-2ch5v10a]
  WATER_PUMP1 = water pump/motor  # not connected
  A3 = VL53lox
  A4 = Soil Moisture Detection Module
  Sensor1 = SEN0114 Moisture sensor  # not connected
  M1 = SHT35-D [package="SIP (Single Inline) [THT]"]
  J1 = Piezo Speaker  # not connected

nets:
  N1: A1.Pin_4, A2.Pin_11
  N2: A1.Pin_5, A2.Pin_12
  N3: A1.Pin_6, A4.DO
  N4: A1.Pin_7, Part2.ALRT
  N5: A1.Pin_40, Part2.SCL, A3.Pin_3, M1.SCL
  N6: A1.Pin_41, Part2.SDA, A3.Pin_4, M1.SDA
  N7: L1.pin_0, Part2.A0
  N8: L1.pin_1, Part2.A1
  VDD: Part2.VDD, A2.Pin_13, A3.Pin_1, A4.VCC, M1.VDD
  GND: Part2.GND, A2.Pin_10, A3.Pin_2, A4.GND, M1.GND
  N9: A2.Pin_2, A2.Pin_5

custom parts:
  Werner Rothschopf (modified to ESP32-S3-DevKitC dual USB by vanepp Aug 2024): ESP32-S3 ESP32-S3-DevKitC-1 Dual USB development board Pyboard CircuitPython Micropython wifi BLE5.0 ESP32-S3.
  sct-013: sct-013 Current transformer. The pcb footprint is from the 3.5mm stereo jack (as the sensor comes with a 3.5 mm stero plug).
  ADS1115: ADC ADS1115
  2-Channel 5v Relay Shield: 2 Channel 5v Relay Shield w. 2x SPD-06VDC-SD-C
  water pump/motor: WATER PUMP BY ARDUBLOCKTR
  VL53lox: VL53L0X Time-of-Flight (ToF) Laser Ranging Sensor Breakout.
  SHT35-D: SHT35-D is an I2C connected temperature and humidity sensor
